// Logisim project 1.circ as structural Verilog: 2 circuits, main circuit half.adder
module half_adder (
  input  A,
  input  B,
  output Sum,
  output Carry
);

  wire nand_1_out;

  xor xor_1 (Sum, A, B);
  nand nand_1 (nand_1_out, B, A);
  nand nand_2 (Carry, nand_1_out, nand_1_out);
endmodule

module full_adder (
  input  A,
  input  B,
  input  C_in,
  output Sum,
  output C_out
);

  wire nand_1_out, nand_2_out, xor_1_out;

  xor xor_1 (xor_1_out, A, B);
  nand nand_1 (nand_1_out, A, B);
  nand nand_2 (nand_2_out, xor_1_out, C_in);
  xor xor_2 (Sum, xor_1_out, C_in);
  nand nand_3 (C_out, nand_2_out, nand_1_out);
endmodule
