// Logisim project 2.circ as structural Verilog: 4 circuits, main circuit main
module main (
  input  M,
  input  A1,
  input  A2,
  input  A3,
  input  A4,
  input  B1,
  input  B2,
  input  B3,
  input  B4,
  output SUM1,
  output SUM2,
  output SUM3,
  output SUM4,
  output C_out
);

  wire xor_1_out, xor_2_out, xor_3_out, xor_4_out;

  xor xor_1 (xor_1_out, B1, M);
  xor xor_2 (xor_2_out, B2, M);
  xor xor_3 (xor_3_out, B3, M);
  xor xor_4 (xor_4_out, B4, M);
  _7483 u_7483_1 (
    .VCC(1'b1), .GND(1'b0), .C_in(M), .A1(A1), .A2(A2), .A3(A3), .A4(A4), .B1(xor_1_out), .B2(xor_2_out),
    .B3(xor_3_out), .B4(xor_4_out), .SUM1(SUM1), .SUM2(SUM2), .SUM3(SUM3), .SUM4(SUM4), .C_out(C_out));
endmodule

module half_adder (
  input  A,
  input  B,
  output Sum,
  output Carry
);

  wire nand_1_out;

  xor xor_1 (Sum, A, B);
  nand nand_1 (nand_1_out, B, A);
  nand nand_2 (Carry, nand_1_out, nand_1_out);
endmodule

module full_adder (
  input  A,
  input  B,
  input  C_in,
  output Sum,
  output C_out
);

  wire nand_1_out, nand_2_out, xor_1_out;

  xor xor_1 (xor_1_out, A, B);
  nand nand_1 (nand_1_out, A, B);
  nand nand_2 (nand_2_out, xor_1_out, C_in);
  xor xor_2 (Sum, xor_1_out, C_in);
  nand nand_3 (C_out, nand_2_out, nand_1_out);
endmodule

module _7483 (
  input  VCC,
  input  GND,
  input  C_in,
  input  A1,
  input  A2,
  input  A3,
  input  A4,
  input  B1,
  input  B2,
  input  B3,
  input  B4,
  output SUM1,
  output SUM2,
  output SUM3,
  output SUM4,
  output C_out
);

  wire full_adder_1_c_out, full_adder_2_c_out, full_adder_3_c_out;

  full_adder full_adder_1 (.A(A1), .B(B1), .C_in(C_in), .Sum(SUM1), .C_out(full_adder_1_c_out));
  full_adder full_adder_2 (.A(A2), .B(B2), .C_in(full_adder_1_c_out), .Sum(SUM2), .C_out(full_adder_2_c_out));
  full_adder full_adder_3 (.A(A3), .B(B3), .C_in(full_adder_2_c_out), .Sum(SUM3), .C_out(full_adder_3_c_out));
  full_adder full_adder_4 (.A(A4), .B(B4), .C_in(full_adder_3_c_out), .Sum(SUM4), .C_out(C_out));

  // Notes on the sheet:
  //   full adder
  //   full adder
  //   full adder
  //   full adder
endmodule
