// Logisim project 2.circ as structural Verilog: 4 circuits, main circuit main
module main (
);

  wire clock_1_out, n7447_1_a_2, n7447_1_b_2, n7447_1_c_2, n7447_1_d_2, n7447_1_e, n7447_1_f, n7447_1_g,
       n7493_1_q1, n7493_1_q2, n7493_1_q3, n7493_1_q4;

  Clock clock_1 (.out(clock_1_out));
  _7493 u_7493_1 (
    .CLK0(clock_1_out), .CLK1(n7493_1_q1), .CLR1(n7493_1_q2), .CLR2(n7493_1_q4), .Q1(n7493_1_q1),
    .Q2(n7493_1_q2), .Q3(n7493_1_q3), .Q4(n7493_1_q4));
  _7447 u_7447_1 (
    .BIRBO(1'b1), .RBI(1'b1), .LT(1'b1), .D(n7493_1_q4), .C(n7493_1_q3), .B(n7493_1_q2), .A(n7493_1_q1),
    .a_2(n7447_1_a_2), .b_2(n7447_1_b_2), .c_2(n7447_1_c_2), .d_2(n7447_1_d_2), .e(n7447_1_e), .f(n7447_1_f),
    .g(n7447_1_g));
  _7_Segment_Display u_7_segment_display_1 (
    .g(n7447_1_g), .f(n7447_1_f), .a(n7447_1_a_2), .b(n7447_1_b_2), .e(n7447_1_e), .d(n7447_1_d_2),
    .c(n7447_1_c_2));  // open: dp
endmodule

module _7447 (
  input  BIRBO,
  input  RBI,
  input  LT,
  input  D,
  input  C,
  input  B,
  input  A,
  output a_2,
  output b_2,
  output c_2,
  output d_2,
  output e,
  output f,
  output g
);

  wire nand_1_out, nand_2_out, nand_3_out, nand_4_out, nand_5_out, nand_6_out, nand_7_out, nand_8_out,
       nand_9_out, nand_10_out, nand_11_out, nand_12_out, nand_13_out, nand_14_out, nand_15_out, nand_16_out,
       nand_17_out, nand_18_out, nand_19_out, nand_20_out, nand_21_out, nand_22_out, nand_23_out,
       nand_24_out, nand_25_out, nand_26_out, nand_27_out, nand_29_out, nand_30_out, nand_31_out,
       nand_32_out, nand_33_out, nand_34_out, nand_35_out, nand_36_out, nand_37_out, nand_38_out,
       nand_39_out, nand_40_out, nand_41_out, nand_42_out, nand_43_out;

  nand nand_1 (nand_1_out, C, C);
  nand nand_2 (nand_2_out, A, A);
  nand nand_3 (nand_3_out, B, B);
  nand nand_4 (nand_4_out, A, A);
  nand nand_5 (nand_5_out, A, A);
  nand nand_6 (nand_6_out, C, C);
  nand nand_7 (nand_7_out, C, C);
  nand nand_8 (nand_8_out, A, A);
  nand nand_9 (nand_9_out, C, C);
  nand nand_10 (nand_10_out, A, A);
  nand nand_11 (nand_11_out, B, B);
  nand nand_12 (nand_12_out, C, C);
  nand nand_13 (nand_13_out, A, A);
  nand nand_14 (nand_14_out, A, A);
  nand nand_15 (nand_15_out, B, B);
  nand nand_16 (nand_16_out, A, A);
  nand nand_17 (nand_17_out, B, B);
  nand nand_18 (nand_18_out, A, A);
  nand nand_19 (nand_19_out, C, C);
  nand nand_20 (nand_20_out, B, B);
  nand nand_21 (nand_21_out, A, A);
  nand nand_22 (nand_22_out, nand_1_out, nand_2_out);
  nand nand_23 (nand_23_out, B, B);
  nand nand_24 (nand_24_out, C, A);
  nand nand_25 (nand_25_out, D, D);
  nand nand_26 (nand_26_out, nand_3_out, nand_4_out);
  nand nand_27 (nand_27_out, B, A);
  nand nand_28 (c_2, B, nand_5_out, nand_6_out);
  nand nand_29 (nand_29_out, nand_7_out, nand_8_out);
  nand nand_30 (nand_30_out, nand_9_out, B);
  nand nand_31 (nand_31_out, B, nand_10_out);
  nand nand_32 (nand_32_out, C, nand_11_out, A);
  nand nand_33 (nand_33_out, D, D);
  nand nand_34 (nand_34_out, nand_12_out, nand_13_out);
  nand nand_35 (nand_35_out, B, nand_14_out);
  nand nand_36 (nand_36_out, nand_15_out, nand_16_out);
  nand nand_37 (nand_37_out, C, nand_17_out);
  nand nand_38 (nand_38_out, C, nand_18_out);
  nand nand_39 (nand_39_out, D, D);
  nand nand_40 (nand_40_out, nand_19_out, B);
  nand nand_41 (nand_41_out, C, nand_20_out);
  nand nand_42 (nand_42_out, C, nand_21_out);
  nand nand_43 (nand_43_out, D, D);
  nand nand_44 (a_2, nand_22_out, nand_23_out, nand_24_out, nand_25_out);
  nand nand_45 (b_2, C, nand_26_out, nand_27_out);
  nand nand_46 (d_2, nand_29_out, nand_30_out, nand_31_out, nand_32_out, nand_33_out);
  nand nand_47 (e, nand_34_out, nand_35_out);
  nand nand_48 (f, nand_36_out, nand_37_out, nand_38_out, nand_39_out);
  nand nand_49 (g, nand_40_out, nand_41_out, nand_42_out, nand_43_out);
endmodule

module D_Flip_Flop (
  input  SET,
  input  D,
  input  CLK,
  input  CLR,
  output Q,
  output R
);

  D_Flip_Flop_part d_ff_1 (.clk(CLK), .D(D), .Q(Q), .Qn(R), .preset(SET), .reset(CLR));  // open: en
endmodule

module _7493 (
  input  CLK0,
  input  CLK1,
  input  CLR1,
  input  CLR2,
  output Q1,
  output Q2,
  output Q3,
  output Q4
);

  wire and_1_out, d_flip_flop_1_r, d_flip_flop_2_r, d_flip_flop_3_r, d_flip_flop_4_r, not_1_out, not_2_out,
       not_3_out, not_4_out;

  not not_1 (not_1_out, CLK0);
  not not_2 (not_2_out, CLK1);
  and and_1 (and_1_out, CLR1, CLR2);
  D_Flip_Flop d_flip_flop_1 (
    .D(d_flip_flop_1_r), .CLK(not_1_out), .CLR(and_1_out), .Q(Q1), .R(d_flip_flop_1_r));  // open: SET
  D_Flip_Flop d_flip_flop_2 (
    .D(d_flip_flop_2_r), .CLK(not_2_out), .CLR(and_1_out), .Q(Q2), .R(d_flip_flop_2_r));  // open: SET
  not not_3 (not_3_out, Q2);
  D_Flip_Flop d_flip_flop_3 (
    .D(d_flip_flop_3_r), .CLK(not_3_out), .CLR(and_1_out), .Q(Q3), .R(d_flip_flop_3_r));  // open: SET
  not not_4 (not_4_out, Q3);
  D_Flip_Flop d_flip_flop_4 (
    .D(d_flip_flop_4_r), .CLK(not_4_out), .CLR(and_1_out), .Q(Q4), .R(d_flip_flop_4_r));  // open: SET
endmodule
