// Logisim project 1.circ as structural Verilog: 3 circuits, main circuit main
module main (
  input  A,
  input  B,
  input  C,
  input  D,
  output P
);

  wire n7404_1__2_1y, n74151_1__5_y, n74151_1__6_w, not_1_out;

  _7404 u_7404_1 (
    ._1_1A(D), ._2_1Y(n7404_1__2_1y), ._7_GND(1'b0), ._14_VCC(1'b1));  // open: _3_2A, _4_2Y, _5_3A, _6_3Y, _13_6A, _12_6Y, _11_5A, _10_5Y, _9_4A, _8_4Y
  and and_1 (P, not_1_out, n74151_1__6_w);
  not not_1 (not_1_out, n74151_1__5_y);
  _74151 u_74151_1 (
    ._1_D3(D), ._2_D2(n7404_1__2_1y), ._3_D1(n7404_1__2_1y), ._4_D0(D), ._5_Y(n74151_1__5_y),
    ._6_W(n74151_1__6_w), ._7_S(1'b0), ._8_GND(1'b0), ._16_VCC(1'b1), ._15_D4(n7404_1__2_1y), ._14_D5(D),
    ._13_D6(D), ._12_D7(n7404_1__2_1y), ._11_A(A), ._10_B(B), ._9_C(C));
endmodule

module _74151 (
  input  _1_D3,
  input  _16_VCC,
  input  _2_D2,
  input  _15_D4,
  input  _3_D1,
  input  _14_D5,
  input  _4_D0,
  input  _13_D6,
  input  _12_D7,
  input  _11_A,
  input  _7_S,
  input  _10_B,
  input  _8_GND,
  input  _9_C,
  output _5_Y,
  output _6_W
);

  wire multiplexer_1_out, not_2_out;

  not not_1 (_5_Y, _6_W);
  or or_1 (_6_W, not_2_out, _7_S);
  Multiplexer #(.select(3), .enable("false")) multiplexer_1 (
    .in0(_4_D0), .in1(_3_D1), .in2(_2_D2), .in3(_1_D3), .in4(_15_D4), .in5(_14_D5), .in6(_13_D6),
    .in7(_12_D7), .out(multiplexer_1_out), .sel({_9_C, _10_B, _11_A}));
  not not_2 (not_2_out, multiplexer_1_out);
endmodule

module _7404 (
  input  _1_1A,
  input  _14_VCC,
  input  _13_6A,
  input  _3_2A,
  input  _11_5A,
  input  _5_3A,
  input  _9_4A,
  input  _7_GND,
  output _2_1Y,
  output _12_6Y,
  output _4_2Y,
  output _10_5Y,
  output _6_3Y,
  output _8_4Y
);

  not not_1 (_2_1Y, _1_1A);
  not not_2 (_4_2Y, _3_2A);
  not not_3 (_6_3Y, _5_3A);
  not not_4 (_12_6Y, _13_6A);
  not not_5 (_10_5Y, _11_5A);
  not not_6 (_8_4Y, _9_4A);
endmodule
