// Logisim project 2.circ as structural Verilog: 1 circuit, main circuit main
module main (
  input  D,
  input  C,
  input  B,
  input  A,
  output P
);

  wire not_1_out, xor_1_out;

  xor xor_1 (xor_1_out, D, C);
  not not_1 (not_1_out, xor_1_out);
  Multiplexer #(.select(2), .enable("false")) multiplexer_1 (
    .in0(not_1_out), .in1(xor_1_out), .in2(xor_1_out), .in3(not_1_out), .out(P), .sel({B, A}));
endmodule
