// Logisim project 3.circ as structural Verilog: 3 circuits, main circuit main
module main (
  input  A,
  input  B,
  output Z1,
  output Z2
);

  wire n74154_1__0, n74154_1__1, n74154_1__2, n74154_1__3, n74154_1__4, n74154_1__5, n74154_1__6,
       n74154_1__7, n74154_1__8, n74154_1__9, n74154_1__10, n74154_1__11, n74154_1__12, n74154_1__13,
       n74154_1__14, n74154_1__15;

  _7430 u_7430_1 (
    ._1A(n74154_1__10), ._1B(n74154_1__8), ._1C(n74154_1__7), ._1D(n74154_1__5), ._1E(n74154_1__2),
    ._1F(n74154_1__0), .GND(1'b0), .VCC(1'b1), ._1H(n74154_1__13), ._1G(n74154_1__15), ._3Y(Z2));  // open: NC, NC_2, NC_3
  _7430 u_7430_2 (
    ._1A(n74154_1__11), ._1B(n74154_1__9), ._1C(n74154_1__6), ._1D(n74154_1__4), ._1E(n74154_1__3),
    ._1F(n74154_1__1), .GND(1'b0), .VCC(1'b1), ._1H(n74154_1__12), ._1G(n74154_1__14), ._3Y(Z1));  // open: NC, NC_2, NC_3
  _74154 u_74154_1 (
    ._0(n74154_1__0), ._1(n74154_1__1), ._2(n74154_1__2), ._3(n74154_1__3), ._4(n74154_1__4),
    ._5(n74154_1__5), ._6(n74154_1__6), ._7(n74154_1__7), ._8(n74154_1__8), ._9(n74154_1__9),
    ._10(n74154_1__10), .GND(1'b0), .VCC(1'b1), .A(A), .B(A), .C(B), .D(B), .G2(1'b0), .G1(1'b0),
    ._15(n74154_1__15), ._14(n74154_1__14), ._13(n74154_1__13), ._12(n74154_1__12), ._11(n74154_1__11));
endmodule

module _74154 (
  input  VCC,
  input  A,
  input  B,
  input  C,
  input  D,
  input  G2,
  input  G1,
  input  GND,
  output _0,
  output _1,
  output _2,
  output _3,
  output _4,
  output _15,
  output _5,
  output _14,
  output _6,
  output _13,
  output _7,
  output _12,
  output _8,
  output _11,
  output _9,
  output _10
);

  wire decoder_1_out0, decoder_1_out1, decoder_1_out2, decoder_1_out3, decoder_1_out4, decoder_1_out5,
       decoder_1_out6, decoder_1_out7, decoder_1_out8, decoder_1_out9, decoder_1_out10, decoder_1_out11,
       decoder_1_out12, decoder_1_out13, decoder_1_out14, decoder_1_out15, nand_12_out;

  nand nand_1 (_0, decoder_1_out0, nand_12_out);
  nand nand_2 (_1, decoder_1_out1, nand_12_out);
  nand nand_3 (_2, decoder_1_out2, nand_12_out);
  nand nand_4 (_3, decoder_1_out3, nand_12_out);
  nand nand_5 (_4, decoder_1_out4, nand_12_out);
  nand nand_6 (_5, decoder_1_out5, nand_12_out);
  nand nand_7 (_6, decoder_1_out6, nand_12_out);
  nand nand_8 (_7, decoder_1_out7, nand_12_out);
  nand nand_9 (_8, decoder_1_out8, nand_12_out);
  nand nand_10 (_9, decoder_1_out9, nand_12_out);
  nand nand_11 (_10, decoder_1_out10, nand_12_out);
  nand nand_12 (nand_12_out, G2, G1);
  Decoder #(.select(4), .enable("false")) decoder_1 (
    .out0(decoder_1_out0), .out1(decoder_1_out1), .out2(decoder_1_out2), .out3(decoder_1_out3),
    .out4(decoder_1_out4), .out5(decoder_1_out5), .out6(decoder_1_out6), .out7(decoder_1_out7),
    .out8(decoder_1_out8), .out9(decoder_1_out9), .out10(decoder_1_out10), .out11(decoder_1_out11),
    .out12(decoder_1_out12), .out13(decoder_1_out13), .out14(decoder_1_out14), .out15(decoder_1_out15),
    .sel({D, C, B, A}));
  nand nand_13 (_15, decoder_1_out15, nand_12_out);
  nand nand_14 (_14, decoder_1_out14, nand_12_out);
  nand nand_15 (_13, decoder_1_out13, nand_12_out);
  nand nand_16 (_12, decoder_1_out12, nand_12_out);
  nand nand_17 (_11, decoder_1_out11, nand_12_out);
endmodule

module _7430 (
  input  _1A,
  input  VCC,
  input  _1B,
  input  NC,
  input  _1C,
  input  _1H,
  input  _1D,
  input  _1G,
  input  _1E,
  input  NC_2,
  input  _1F,
  input  NC_3,
  input  GND,
  output _3Y
);

  nand nand_1 (_3Y, _1F, _1E, _1D, _1C, _1B, _1A, _1H, _1G);
endmodule
