// Logisim project 4.circ as structural Verilog: 1 circuit, main circuit main
module main (
  input  A,
  input  B,
  output Z1,
  output Z2
);

  wire decoder_1_out0, decoder_1_out1, decoder_1_out2, decoder_1_out3, decoder_1_out4, decoder_1_out5,
       decoder_1_out6, decoder_1_out7;

  or or_1 (Z2, decoder_1_out2, decoder_1_out3, decoder_1_out0, decoder_1_out7);
  or or_2 (Z1, decoder_1_out1, decoder_1_out5, decoder_1_out4, decoder_1_out6);
  Decoder #(.select(3), .enable("false")) decoder_1 (
    .out0(decoder_1_out0), .out1(decoder_1_out1), .out2(decoder_1_out2), .out3(decoder_1_out3),
    .out4(decoder_1_out4), .out5(decoder_1_out5), .out6(decoder_1_out6), .out7(decoder_1_out7),
    .sel({{2{B}}, A}));
endmodule
