// Logisim project 1.1.circ as structural Verilog: 1 circuit, main circuit main
module main (
  input  S1_1,
  input  S1_2,
  input  S2_1,
  input  S2_2,
  input  S3_1,
  input  S3_2,
  input  S4_1,
  input  S4_1_2,
  input  S5_1,
  input  S5_2
);

  wire and_1_out, nand_1_out, nor_1_out, or_1_out, xor_1_out;

  and and_1 (and_1_out, S1_1, S1_2);
  nand nand_1 (nand_1_out, S2_1, S2_2);
  or or_1 (or_1_out, S3_1, S3_2);
  nor nor_1 (nor_1_out, S4_1, S4_1_2);
  xor xor_1 (xor_1_out, S5_1, S5_2);
  LED led_1 (.in(and_1_out));
  LED led_2 (.in(nand_1_out));
  LED led_3 (.in(or_1_out));
  LED led_4 (.in(nor_1_out));
  LED led_5 (.in(xor_1_out));

  // Notes on the sheet:
  //   LED-1
  //   LED-2
  //   LED-3
  //   LED-4
  //   LED-5
endmodule
