// Logisim project 1.4.circ as structural Verilog: 1 circuit, main circuit main
module main (
  input  S1_1
);

  wire not_1_out;

  not not_1 (not_1_out, S1_1);
  LED led_1 (.in(not_1_out));

  // Notes on the sheet:
  //   LED-1
endmodule
