// Logisim project 2.circ as structural Verilog: 1 circuit, main circuit main
module main (
  input  A,
  input  B,
  input  A_2,
  input  B_2,
  output E,
  output D
);

  wire nand_1_out, nand_2_out, nor_1_out;

  nand nand_1 (nand_1_out, A, B);
  nor nor_1 (nor_1_out, A, B);
  nand nand_2 (nand_2_out, B_2, B_2);
  xor xor_1 (E, nor_1_out, nand_1_out);
  nand nand_3 (D, A_2, nand_2_out);

  // Notes on the sheet:
  //   C
  //   D
  //   C
endmodule
