// Logisim project 3.2.circ as structural Verilog: 1 circuit, main circuit main
module main (
  input  DOOR_1,
  input  DOOR_2,
  input  DOOR_3,
  input  DOOR_4,
  output ALARM
);

  nor nor_1 (ALARM, DOOR_2, DOOR_1, DOOR_4, DOOR_3);
endmodule
