// Logisim project 2.circ as structural Verilog: 1 circuit, main circuit main
module main (
  input  D,
  input  C,
  output Q,
  output out_4
);

  wire nand_1_out, nand_2_out, not_1_out;

  not not_1 (not_1_out, D);
  nand nand_1 (nand_1_out, D, C);
  nand nand_2 (nand_2_out, C, not_1_out);
  nand nand_3 (Q, nand_1_out, out_4);
  nand nand_4 (out_4, Q, nand_2_out);
endmodule
