// Logisim project 3.circ as structural Verilog: 3 circuits, main circuit main
module main (
  input  PRESET1,
  input  J1,
  input  K1,
  input  CLEAR1,
  output Q1,
  output Q_prime_1
);

  wire CLOCK1_out;

  Clock CLOCK1 (.out(CLOCK1_out));
  _7476 u_7476_1 (
    .VCC(1'b1), .PRESET1(PRESET1), .J1(J1), .CLOCK1(CLOCK1_out), .K1(K1), .CLEAR1(CLEAR1), .GND(1'b0),
    .Q1(Q1), .Q1_prime(Q_prime_1));  // open: PRESET2, J2, CLOCK2, K2, CLEAR2, Q2, Q2_prime
endmodule

module JK_Flip_Flop (
  input  PRESET,
  input  J,
  input  CLOCK,
  input  K,
  input  CLEAR,
  output Q,
  output Q_prime
);

  wire nand_1_out, nand_2_out, nand_3_out, nand_4_out, nand_5_out, nand_6_out, not_1_out;

  nand nand_1 (nand_1_out, J, CLOCK);
  nand nand_2 (nand_2_out, CLOCK, K);
  not not_1 (not_1_out, CLOCK);
  nand nand_3 (nand_3_out, PRESET, nand_1_out);
  nand nand_4 (nand_4_out, nand_3_out, nand_2_out, CLEAR);
  nand nand_5 (nand_5_out, nand_3_out, not_1_out);
  nand nand_6 (nand_6_out, not_1_out, nand_4_out);
  nand nand_7 (Q, PRESET, nand_5_out, Q_prime);
  nand nand_8 (Q_prime, Q, nand_6_out, CLEAR);
endmodule

module _7476 (
  input  VCC,
  input  PRESET1,
  input  J1,
  input  CLOCK1,
  input  K1,
  input  CLEAR1,
  input  PRESET2,
  input  J2,
  input  CLOCK2,
  input  K2,
  input  CLEAR2,
  input  GND,
  output Q1,
  output Q1_prime,
  output Q2,
  output Q2_prime
);

  JK_Flip_Flop jk_flip_flop_1 (
    .PRESET(PRESET1), .J(J1), .CLOCK(CLOCK1), .K(K1), .CLEAR(CLEAR1), .Q(Q1), .Q_prime(Q1_prime));
  JK_Flip_Flop jk_flip_flop_2 (
    .PRESET(PRESET2), .J(J2), .CLOCK(CLOCK2), .K(K2), .CLEAR(CLEAR2), .Q(Q2), .Q_prime(Q2_prime));
endmodule
