// Logisim project 4.circ as structural Verilog: 3 circuits, main circuit main
module main (
  input  CLR,
  input  D,
  input  CLK,
  input  PR,
  output Q,
  output Q_prime
);

  _7474 u_7474_1 (
    ._1__CLR1(CLR), ._2__D1(D), ._3__CLK1(CLK), ._4__PR1(PR), ._5__Q1(Q), ._6__nQ1(Q_prime));  // open: _7__GND, _14__VCC, _13__CLR2, _12__D2, _11__CLK2, _10__PR2, _9__Q2, _8__nQ2
endmodule

module _7474 (
  input  _1__CLR1,
  input  _14__VCC,
  input  _2__D1,
  input  _13__CLR2,
  input  _3__CLK1,
  input  _12__D2,
  input  _4__PR1,
  input  _11__CLK2,
  input  _10__PR2,
  input  _7__GND,
  output _5__Q1,
  output _6__nQ1,
  output _9__Q2,
  output _8__nQ2
);

  D_Flip_Flop d_flip_flop_1 (
    .PRESET(_4__PR1), .D(_2__D1), .CLOCK(_3__CLK1), .CLEAR(_1__CLR1), .Q(_5__Q1), .Q_prime(_6__nQ1));
  D_Flip_Flop d_flip_flop_2 (
    .PRESET(_10__PR2), .D(_12__D2), .CLOCK(_11__CLK2), .CLEAR(_13__CLR2), .Q(_9__Q2), .Q_prime(_8__nQ2));
endmodule

module D_Flip_Flop (
  input  PRESET,
  input  D,
  input  CLOCK,
  input  CLEAR,
  output Q,
  output Q_prime
);

  wire nand_1_out, nand_2_out, nand_3_out, nand_4_out, nand_5_out, nand_6_out, not_1_out, not_2_out;

  not not_1 (not_1_out, D);
  nand nand_1 (nand_1_out, D, CLOCK);
  nand nand_2 (nand_2_out, CLOCK, not_1_out);
  not not_2 (not_2_out, CLOCK);
  nand nand_3 (nand_3_out, PRESET, nand_1_out, nand_4_out);
  nand nand_4 (nand_4_out, nand_3_out, nand_2_out, CLEAR);
  nand nand_5 (nand_5_out, nand_3_out, not_2_out);
  nand nand_6 (nand_6_out, not_2_out, nand_4_out);
  nand nand_7 (Q, PRESET, nand_5_out, Q_prime);
  nand nand_8 (Q_prime, Q, nand_6_out, CLEAR);
endmodule
